// Logisim project asm_to_ram.circ as structural Verilog: 1 circuit, main circuit main
module main (
);

  wire clock_1_out, mips_alu_2_p4;
  wire [31:0] mips_alu_1_p4, mipsprogramrom_1_p2, register_1_q, shifter_1_out;

  Clock clock_1 (.out(clock_1_out));
  Register #(.width(32)) register_1 (
    .D(mips_alu_1_p4), .en(mips_alu_2_p4), .Q(register_1_q), .clk(clock_1_out));  // open: clr
  Shifter #(.width(32), .shift("lr")) shifter_1 (.in(register_1_q), .\dist (5'b00010), .out(shifter_1_out));
  // MIPSProgramROM mipsprogramrom_1: pin names not known; wires that end beside it: register_1_q, mipsprogramrom_1_p2
  // MIPS_ALU mips_alu_1: pin names not known; wires that end beside it: register_1_q, 32'h4, 4'b0010, mips_alu_1_p4
  RAM #(.addrWidth(24), .dataWidth(32), .bus("separate")) ram_1 (
    .addr(shifter_1_out[23:0]), .din(mipsprogramrom_1_p2), .str(mips_alu_2_p4), .clk(clock_1_out));  // open: data, sel, ld, clr
  // MIPS_ALU mips_alu_2: pin names not known; wires that end beside it: register_1_q, 32'h3c, 4'b0111, mips_alu_2_p4

  // Notes on the sheet:
  //   (1)
  //   (2)
  //   Klik på (1) Enheden
  //   Load en .asm fil
  //   Ctrl-R
  //   Ctrl-K
  //   Simulate > Tick Frequency > Noget højt
  //   skriv sidste intruktions addresse nummer i (2)
endmodule
