// Logisim project file.circ as structural Verilog: 3 circuits, main circuit main
module main (
);

  wire mips_alu_2_p3, mips_alu_3_p5, not_1_out, registerfile_1_p5, Run_Instr, undriven, undriven_2;
  wire [4:0] instr_rW, lw_rW, multiplexer_2_out_2, multiplexer_4_out;
  wire [5:0] instr__0_5;
  wire [25:6] multiplexer_2_out;
  wire [27:0] shifter_2_out;
  wire [31:0] ALU_Result, bit_extender_1_out, lw_sw_Addr, mips_alu_1_p4, mips_alu_3_p4, multiplexer_1_out,
       multiplexer_3_out, multiplexer_6_out, multiplexer_7_out, multiplexer_8_out, ram_1_data, Reg_B_Value,
       register_1_q, shifter_1_out, shifter_3_out, sw_Data;
  wire [31:26] multiplexer_2_out_3;

  Register #(.width(32)) register_1 (.D(multiplexer_8_out), .en(Run_Instr), .Q(register_1_q));  // open: clk, clr
  Register #(.width(1)) Run_Instr_Next (.D(undriven), .Q(Run_Instr));  // open: en, clk, clr
  Register #(.width(1)) Store (.D(undriven_2));  // open: en, Q, clk, clr
  Register #(.width(32)) u_sw_Data (.D(Reg_B_Value), .Q(sw_Data));  // open: en, clk, clr
  Register #(.width(32)) Addr (.D(ALU_Result), .Q(lw_sw_Addr));  // open: en, clk, clr
  Register #(.width(5)) u_lw_rW (.D(instr_rW), .Q(lw_rW));  // open: en, clk, clr
  Multiplexer #(.width(32), .enable("false")) multiplexer_1 (
    .in0(lw_sw_Addr), .in1(shifter_1_out), .out(multiplexer_1_out), .sel(Run_Instr));
  Shifter #(.width(32), .shift("lr")) shifter_1 (.in(register_1_q), .\dist (5'b00010), .out(shifter_1_out));
  RAM #(.addrWidth(24), .dataWidth(32), .bus("separate")) ram_1 (
    .addr(multiplexer_1_out[23:0]), .din(sw_Data), .data(ram_1_data));  // open: str, sel, clk, ld, clr
  // MIPS_ALU mips_alu_1: pin names not known; wires that end beside it: register_1_q, 32'h4, 4'b0010, mips_alu_1_p4
  Multiplexer #(.width(32), .enable("false")) multiplexer_2 (
    .in0({32{1'b0}}), .in1(ram_1_data),
    .out({multiplexer_2_out_3, multiplexer_2_out[25:21], multiplexer_2_out_2, multiplexer_2_out[15:6], instr__0_5}),
    .sel(Run_Instr));
  Multiplexer #(.width(32), .enable("false")) multiplexer_3 (
    .in0({multiplexer_2_out_3, multiplexer_2_out[25:21], multiplexer_2_out_2, multiplexer_2_out[15:6], instr__0_5}),
    .in1(ALU_Result), .out(multiplexer_3_out), .sel(Run_Instr));
  Shifter #(.width(28)) shifter_2 (
    .in({2'b00, multiplexer_2_out[25:21], multiplexer_2_out_2, multiplexer_2_out[15:6], instr__0_5}),
    .\dist (5'b00010), .out(shifter_2_out));
  Multiplexer #(.width(5), .enable("false")) multiplexer_4 (
    .in0(lw_rW), .in1(instr_rW), .out(multiplexer_4_out), .sel(Run_Instr));
  Multiplexer #(.width(5), .enable("false")) multiplexer_5 (
    .in0(multiplexer_2_out[15:11]), .in1(multiplexer_2_out_2), .out(instr_rW));  // open: sel
  assign bit_extender_1_out = {{16{multiplexer_2_out[15]}}, {multiplexer_2_out[15:6], instr__0_5}};  // Bit_Extender bit_extender_1
  // RegisterFile registerfile_1: pin names not known; wires that end beside it: multiplexer_3_out, multiplexer_4_out, multiplexer_2_out[25:21], multiplexer_2_out_2, registerfile_1_p5, Reg_B_Value
  Control control_1 (.Instruction_31_26(multiplexer_2_out_3));  // open: RegDst, ALUsrc, MemtoReg, RegWrite, MemRead, MemWrite, Branch, ALUOp
  Multiplexer #(.width(32), .enable("false")) multiplexer_6 (
    .in0(bit_extender_1_out), .in1(Reg_B_Value), .out(multiplexer_6_out));  // open: sel
  Shifter #(.width(32)) shifter_3 (.in(bit_extender_1_out), .\dist (5'b00010), .out(shifter_3_out));
  // MIPS_ALU mips_alu_2: pin names not known; wires that end beside it: registerfile_1_p5, multiplexer_6_out, mips_alu_2_p3, ALU_Result
  // MIPS_ALU mips_alu_3: pin names not known; wires that end beside it: mips_alu_1_p4, shifter_3_out, 4'b0010, mips_alu_3_p4, mips_alu_3_p5
  Multiplexer #(.width(32), .enable("false")) multiplexer_7 (
    .in0(mips_alu_1_p4), .in1(mips_alu_3_p4), .out(multiplexer_7_out));  // open: sel
  Multiplexer #(.width(32), .enable("false")) multiplexer_8 (
    .in0({mips_alu_1_p4[31:28], shifter_2_out}), .in1(multiplexer_7_out), .out(multiplexer_8_out),
    .sel(not_1_out));
  not not_1 (not_1_out, mips_alu_3_p5);

  // Notes on the sheet:
  //   from control
  //   from control
  //   PC
  //   Should Run Instruction
  //   Control
  //   Alu Control
  //   Should Jump
endmodule

module Control (
  input  [5:0] Instruction_31_26,
  output RegDst,
  output ALUsrc,
  output MemtoReg,
  output RegWrite,
  output MemRead,
  output MemWrite,
  output Branch,
  output [1:0] ALUOp
);

  wire Jump;

  // PLA Control: pin names not known; wires that end beside it: Instruction_31_26, {RegDst, ALUsrc, MemtoReg, RegWrite, MemRead, MemWrite, Branch, ALUOp}, Jump
endmodule

module ALU_control (
  input  [1:0] ALUOp,
  input  [5:0] Funct,
  output [3:0] ALUctrl
);

  // PLA ALU_ctrl: pin names not known; wires that end beside it: {ALUOp, Funct}, ALUctrl
endmodule
